# Fritzing sketch ScrubBot (saved by Fritzing 0.9.0b)
circuit board: 8.46667cm x 5.64444cm
breadboards: 1

parts:
  Part1 = Arduino Mega 2560 (Rev3)
  J1 = Basic Servo
  J2 = Basic Servo
  S1 = Pushbutton [package=THT]
  VCC1 = 4 x AAA Battery Mount
  VCC2 = Battery block 9V
  LED1 = LED - 5mm [color="Infrared (850nm)" package="5 mm [THT]"]
  LED2 = LED - 5mm [color="Infrared (850nm)" package="5 mm [THT]"]
  LED3 = LED - 5mm [color="Infrared (850nm)" package="5 mm [THT]"]
  R1 = Resistor [tolerance=±5% resistance=330 package=THT]
  R2 = Resistor [tolerance=±5% resistance=330 package=THT]
  R3 = Resistor [tolerance=±5% resistance=330 package=THT]
  R4 = Resistor [tolerance=±5% resistance=100k package=THT]
  R5 = Resistor [tolerance=±5% resistance=100k package=THT]
  R6 = Resistor [tolerance=±5% resistance=100k package=THT]
  R7 = Resistor [tolerance=±5% resistance=2.2k package=THT]
  R8 = Resistor [tolerance=±5% resistance=2.2k package=THT]
  R9 = Resistor [tolerance=±5% resistance=2.2k package=THT]
  P1 = S1133 Si Photodiode [package="8mm Ceramic [THT]"]
  P2 = S1133 Si Photodiode [package="8mm Ceramic [THT]"]
  P3 = S1133 Si Photodiode [package="8mm Ceramic [THT]"]

nets:
  N1: Part1.A13, R4.Pin_1, P1.cathode
  N2: Part1.A14, R5.Pin_1, P2.cathode
  N3: Part1.A15, R6.Pin_1, P3.cathode
  GND: Part1.GND, J1.gnd, J2.gnd, S1.leg1, VCC1.-, VCC2.-, LED1.cathode, LED2.cathode, LED3.cathode, R4.Pin_0, R5.Pin_0, R6.Pin_0
  N4: Part1.VIN, VCC2.+
  N5: Part1.D2_PWM, J2.pulse
  N6: Part1.D4_PWM, J1.pulse
  N7: Part1.D45, S1.leg0
  N8: Part1.D46, R1.Pin_0, R7.Pin_1
  N9: Part1.D48, R2.Pin_0, R8.Pin_1
  N10: Part1.D50, R3.Pin_0, R9.Pin_1
  VCC: J1.vcc, J2.vcc, VCC1.+
  N11: LED1.anode, R1.Pin_1
  N12: LED2.anode, R2.Pin_1
  N13: LED3.anode, R3.Pin_1
  N14: R7.Pin_0, P1.anode
  N15: R8.Pin_0, P2.anode
  N16: R9.Pin_0, P3.anode

notes:
  ScrubBot, bot schematic overview, 0.1
  left wheel
  right wheel
  (4) AAA pack
  left
  center
  right
  bump button
